# Fritzing sketch LaspelyArduino-Schematic (saved by Fritzing 0.8.7b)
breadboards: 1

parts:
  µDuino = Arduino Uno (Rev3)
  R1 = Resistor [tolerance=±5% resistance=1M package=THT]
  R2 = Resistor [tolerance=±5% resistance=1M package=THT]
  LETSGO_switch = SWITCH_SPDT [package=kps-1290]
  ON/OFF_switch = SWITCH-SPST-2 [package=switch-spst-vertical]
  R3 = Resistor [tolerance=±5% resistance=1M package=THT]
  IC1 = Voltage Regulator [package=to220-igo]
  VCC1 = Battery block 9V
  S1 = Pushbutton [package=THT]
  S2 = Pushbutton [package=THT]

nets:
  LOAD pour l'afficheur: µDuino.D10_PWM/SS
  CLOCK pour l'afficheur: µDuino.D11_PWM/MOSI
  DATAIN pour l'afficheur: µDuino.D12/MISO
  GND: µDuino.GND, R1.Pin_1, R2.Pin_1, R3.Pin_1, IC1.GND, VCC1.-, S1.leg0, S2.leg0
  N1: µDuino.D2, R1.Pin_0
  N2: µDuino.D3_PWM, R2.Pin_0
  N3: µDuino.D4, LETSGO_switch.P
  N4: µDuino.5V, LETSGO_switch.O, IC1.OUT, S1.leg1, S2.leg1
  N5: LETSGO_switch.S, R3.Pin_0
  N6: ON/OFF_switch.O, VCC1.+
  N7: ON/OFF_switch.P, IC1.IN
